# Fritzing sketch SA2HoTT (saved by Fritzing 0.9.1b)

parts:
  Bauteil1 = Arduino Pro Mini v13
  J1 = female pin header, 3 pins [form="♀ (female)" part_number=Empfänger]
  R1 = Resistor [tolerance=±0.05% resistance=1.8k package=THT]
  D1 = Zener Diode [part_number="Z-Diode 3,3V" breakdown_voltage=3.3V package="Melf DO-213 AB [SMD]"]
  J2 = female pin header, 1 pin [form="♀ (female)" part_number="Spannung 0-5V"]
  J3 = rounded female pin header, 1 pin [form="♀ (female rounded)" part_number="Strom 0-5V"]
  R2 = Resistor [tolerance=±0.05% resistance=1k package=THT]
  R3 = Resistor [tolerance=±0.05% resistance=1k package=THT]
  J4 = female pin header, 1 pin [form="♀ (female)" part_number="Smart Audio TBS"]

nets:
  N1: Bauteil1.RAW, J1.pin2
  N2: Bauteil1.GND, J1.pin1, D1.anode
  N3: Bauteil1.A1, J3.pin1
  N4: Bauteil1.A0, J2.pin1
  N5: Bauteil1.D3_PWM, R1.Pin_1
  N6: Bauteil1.D1/RX, R3.Pin_1
  N7: Bauteil1.D0/TX, R2.Pin_1
  N8: J1.pin3, R1.Pin_0, D1.cathode
  N9: R2.Pin_0, R3.Pin_0, J4.pin1

notes:
  -
  +
  T
